# Fritzing sketch LightSensor (saved by Fritzing 0.9.3b)
breadboards: 1

parts:
  元件1 = LinkIt 7697
  R1 = Photocell (LDR) [package=THT]
  R2 = Resistor [tolerance=±5% resistance=220 package="2512 [SMD]"]
  LED1 = LED - 5mm [color="Red (633nm)" package="5 mm [THT]"]  # not connected

nets:
  N1: 元件1.P16, 元件1.RTC_PWR_POS, R1.pin_0, R2.Pin_1
  N2: 元件1.P17, 元件1.GND, 元件1.RTC_PWR_NEG, R2.Pin_0
  N3: 元件1.5V, R1.pin_1

custom parts:
  LinkIt 7697: LinkIt 7697 is an IoT development board based on MT7697, supporting Wi-Fi and Bluetooth Low Energy connectivity.
