# Fritzing sketch Servosweep (saved by Fritzing 0.9.3b)
breadboards: 1

parts:
  元件1 = LinkIt 7697
  J1 = Basic Servo

nets:
  N1: 元件1.P16, 元件1.RTC_PWR_POS
  GND: 元件1.GND, 元件1.RTC_PWR_NEG, J1.gnd
  5V: 元件1.5V, J1.vcc

custom parts:
  LinkIt 7697: LinkIt 7697 is an IoT development board based on MT7697, supporting Wi-Fi and Bluetooth Low Energy connectivity.
